# Fritzing sketch Aufsatzboard (saved by Fritzing 0.9.3b)
circuit board: 2.6cm x 4cm
breadboards: 1

parts:
  J2 = female pin header, 10 pins [form="♀ (female)"]
  J3 = female pin header, 10 pins [form="♀ (female)"]
  J4 = female pin header, 2 pins [form="♀ (female)"]
  J6 = female pin header, 4 pins [form="♀ (female)"]
  J5 = female pin header, 4 pins [form="♀ (female)"]

nets:
  N1: J2.pin1, J5.pin1
  N2: J2.pin7, J6.pin2
  N3: J2.pin8, J6.pin1
  N4: J2.pin9, J6.pin3, J5.pin4
  N5: J2.pin10, J6.pin4
  N6: J3.pin1, J5.pin3
  N7: J3.pin5, J5.pin2
  N8: J3.pin7, J4.pin2
  N9: J3.pin10, J4.pin1

notes:
  GND VCC SCL SCA
  Tare
  VCC SCK DT GND
  Display
  HX711
